# Fritzing sketch TamagotchiESP32_schematic (saved by Fritzing 1.0.3b)
breadboards: 1

parts:
  S1 = Pushbutton [package="[THT]"]
  S2 = Pushbutton [package="[THT]"]
  S3 = Pushbutton [package="[THT]"]
  R1 = Resistor [tolerance=±5% resistance=220 package="0402 [SMD]"]
  R2 = Resistor [tolerance=±5% resistance=220 package="0402 [SMD]"]
  R3 = Resistor [tolerance=±5% resistance=220 package="0402 [SMD]"]
  U1 = ESP32-38PinWide [part_number=ESP32-38PinWide]
  OLED1 = OLED 128x64 I2C Monochrome Display
  J1 = Piezo Speaker

nets:
  N1: S1.Pin_1, R1.Pin_1, U1.GPIO23
  GND: S1.Pin_3, S2.Pin_3, S3.Pin_3, U1.GND, OLED1.GND, J1.pin1
  N2: S2.Pin_1, R2.Pin_1, U1.GPIO19
  N3: S3.Pin_1, R3.Pin_1, U1.GPIO18
  N4: R1.Pin_0, R2.Pin_0, R3.Pin_0, U1.3.3, OLED1.VDD
  N5: U1.GPIO15, J1.pin2
  N6: U1.GPIO21, OLED1.SDA
  N7: U1.GPIO22, OLED1.SCK

custom parts:
  ESP32-38PinWide: Generic 38-Pin ESP32 with wide format (only access to one side of pins on a breadboard) based on Stephen Lilley's HiLetgo ESP-WROOM-32 ESP32 ESP-32S Development Board.
